// Logisim project ader.circ as structural Verilog: 1 circuit, main circuit main
module main (
);

  wire and_1_out, and_2_out, and_3_out, and_4_out, or_1_out, or_2_out, undriven, undriven_2, undriven_3,
       undriven_4, undriven_5, xor_1_out, xor_2_out, xor_3_out, xor_4_out;

  xor xor_1 (xor_1_out, undriven, undriven_2);
  and and_1 (and_1_out, undriven, undriven_2);
  xor xor_2 (xor_2_out, undriven_3, undriven_4);
  and and_2 (and_2_out, undriven_3, undriven_4);
  and and_3 (and_3_out, xor_1_out, undriven_5);
  and and_4 (and_4_out, xor_2_out, or_1_out);
  xor xor_3 (xor_3_out, xor_1_out, undriven_5);
  or or_1 (or_1_out, and_3_out, and_1_out);
  xor xor_4 (xor_4_out, xor_2_out, or_1_out);
  or or_2 (or_2_out, and_4_out, and_2_out);
endmodule
